// Logisim project CPU 8 bits Logisim.circ as structural Verilog: 16 circuits, main circuit CPU
module RAM (
  input  [7:0] DATA,
  input  [3:0] ADDRESS,
  input  Write,
  input  Clock,
  input  On_Stop,
  output [7:0] Load_Store_Data
);

  wire Clear_out, not_1_out;

  Button Clear (.out(Clear_out));
  assign Load_Store_Data = Write ? DATA : 8'bz;  // Controlled_Buffer controlled_buffer_1
  not not_1 (not_1_out, Write);
  RAM_part #(.addrWidth(4)) ram_1 (
    .addr(ADDRESS), .data(Load_Store_Data), .sel(On_Stop), .clk(Clock), .ld(not_1_out), .clr(Clear_out));
endmodule

module SOMADOR_SUBTRADOR (
  input  A,
  input  B,
  input  Te,
  input  M,
  output S,
  output TS
);

  wire and_1_out, and_2_out, or_1_out, xor_1_out, xor_2_out;

  xor xor_1 (xor_1_out, A, B);
  and and_1 (and_1_out, Te, B);
  xor xor_2 (xor_2_out, M, A);
  or or_1 (or_1_out, B, Te);
  and and_2 (and_2_out, xor_2_out, or_1_out);
  xor xor_3 (S, xor_1_out, Te);
  or or_2 (TS, and_1_out, and_2_out);
endmodule

module BANCO_DE_REGISTRADORES_3 (
  input  [7:0] Ent__Dados,
  input  [2:0] Sel__Reg,
  input  Enable_Reg,
  input  [2:0] Sel__Saida,
  input  Clock_Reg,
  input  Clear,
  input  [2:0] Sel__Clock,
  output [7:0] Saida
);

  wire demultiplexer_2_out0, demultiplexer_2_out1, demultiplexer_2_out2, demultiplexer_2_out3,
       demultiplexer_2_out4;
  wire [7:0] demultiplexer_1_out1, demultiplexer_1_out2, demultiplexer_1_out3, demultiplexer_1_out4,
       demultiplexer_1_out5, R0_q, R1_q, R2_q, R3_q;

  Demultiplexer #(.select(3), .width(8), .enable("false")) demultiplexer_1 (
    .out1(demultiplexer_1_out1), .out2(demultiplexer_1_out2), .out3(demultiplexer_1_out3),
    .out4(demultiplexer_1_out4), .out5(demultiplexer_1_out5), .out6(demultiplexer_1_out5),
    .out7(demultiplexer_1_out5), .in(Ent__Dados), .sel(Sel__Reg));  // open: out0
  Demultiplexer #(.select(3), .enable("false")) demultiplexer_2 (
    .out0(demultiplexer_2_out0), .out1(demultiplexer_2_out1), .out2(demultiplexer_2_out2),
    .out3(demultiplexer_2_out3), .out4(demultiplexer_2_out4), .out5(demultiplexer_2_out0),
    .out6(demultiplexer_2_out0), .out7(demultiplexer_2_out0), .in(Clock_Reg), .sel(Sel__Clock));
  Register R0 (.D(demultiplexer_1_out1), .en(Enable_Reg), .Q(R0_q), .clk(demultiplexer_2_out1), .clr(Clear));
  Register R1 (.D(demultiplexer_1_out2), .en(Enable_Reg), .Q(R1_q), .clk(demultiplexer_2_out2), .clr(Clear));
  Register R2 (.D(demultiplexer_1_out3), .en(Enable_Reg), .Q(R2_q), .clk(demultiplexer_2_out3), .clr(Clear));
  Register R3 (.D(demultiplexer_1_out4), .en(Enable_Reg), .Q(R3_q), .clk(demultiplexer_2_out4), .clr(Clear));
  Multiplexer #(.select(3), .width(8), .enable("false")) multiplexer_1 (
    .in0({8{1'b0}}), .in1(R0_q), .in2(R1_q), .in3(R2_q), .in5({8{1'b0}}), .in7({8{1'b0}}), .out(Saida),
    .sel(Sel__Saida));  // open: in4, in6
  // also tied to GND on the sheet: {demultiplexer_1_out5[0], demultiplexer_1_out5[1], demultiplexer_1_out5[2], demultiplexer_1_out5[3], demultiplexer_1_out5[4], demultiplexer_1_out5[5], demultiplexer_1_out5[6], demultiplexer_1_out5[7], demultiplexer_2_out0}
endmodule

// ULA
module ULA (
  input  [7:0] Rx,
  input  [7:0] Ry,
  output [7:0] \Saída_1 
);

  Adder adder_1 (.a(Rx), .b(Ry), .out(\Saída_1 ));  // open: cin, cout
endmodule

module IR (
  input  [7:0] Entr__IR,
  input  IR_Load,
  input  Clock,
  output [7:0] Op__Code,
  output [1:0] Ry,
  output [1:0] Rx
);

  Register register_1 (.D(Entr__IR), .en(IR_Load), .Q(Op__Code), .clk(Clock));  // open: clr

  assign Rx = Op__Code[5:4];
  assign Ry = Op__Code[7:6];
endmodule

module PC (
  input  [7:0] Next_Value,
  input  [1:0] Sel,
  input  PC_Load,
  input  Clock,
  input  PC_Clear,
  output [7:0] saida
);

  wire [7:0] adder_1_out, adder_2_out, multiplexer_1_out;

  Adder adder_1 (.a(saida), .b(8'h1), .out(adder_1_out));  // open: cin, cout
  Adder adder_2 (.a(saida), .b({8{1'b0}}), .out(adder_2_out));  // open: cin, cout
  Multiplexer #(.select(2), .width(8), .enable("false")) multiplexer_1 (
    .in0(adder_1_out), .in1(Next_Value), .in2(adder_2_out), .out(multiplexer_1_out), .sel(Sel));  // open: in3
  Register PC (.D(multiplexer_1_out), .en(PC_Load), .Q(saida), .clk(Clock), .clr(PC_Clear));
endmodule

module MEMORIA_DE_DADOS (
  input  [7:0] in_1,
  input  in_2,
  input  in_3,
  input  [7:0] in_4,
  output [7:0] out_5,
  output [7:0] out_6
);

  wire clock_1_out, not_1_out;

  Clock clock_1 (.out(clock_1_out));
  assign out_5 = in_2 ? in_1 : 8'bz;  // Controlled_Buffer controlled_buffer_1
  not not_1 (not_1_out, in_2);
  Controlled_Buffer #(.width(8)) controlled_buffer_2 ();  // open: in, out, en
  RAM_part ram_1 (.addr(in_1), .data(out_5), .clk(clock_1_out), .ld(not_1_out), .clr(in_3));  // open: sel
  ROM rom_1 (.data(in_4));  // open: addr, sel
  Hex_Digit_Display hex_digit_display_1 (.value(out_5[3:0]));  // open: dp
  Hex_Digit_Display hex_digit_display_2 (.value(out_5[7:4]));  // open: dp

  assign out_6 = in_4;
endmodule

// B. REG
module BANCO_DE_REGISTRADORES (
  input  [7:0] Ent__Registradores,
  input  Enable,
  input  [1:0] Sel_Saida_Rx,
  input  Clock,
  input  [1:0] Sel_Saida_Ry,
  input  Clear,
  input  Enable_Saida_Reg,
  output [7:0] Saida_Rx,
  output [7:0] Saida_Ry
);

  wire [7:0] R0_q, R1_q, R2_q, R3_q;

  Register R0 (.D(Ent__Registradores), .en(Enable), .Q(R0_q), .clk(Clock), .clr(Clear));
  Register R1 (.D(R0_q), .en(Enable), .Q(R1_q), .clk(Clock));  // open: clr
  Register R2 (.D(R1_q), .en(Enable), .Q(R2_q), .clk(Clock));  // open: clr
  Register R3 (.D(R2_q), .en(Enable), .Q(R3_q), .clk(Clock), .clr(Clear));
  Multiplexer #(.select(2), .width(8)) multiplexer_1 (
    .in0(R0_q), .in1(R1_q), .in2(R2_q), .in3(R3_q), .out(Saida_Rx), .sel(Sel_Saida_Rx), .en(Enable_Saida_Reg));
  Multiplexer #(.select(2), .width(8)) multiplexer_2 (
    .in0(R0_q), .in1(R1_q), .in2(R2_q), .in3(R3_q), .out(Saida_Ry), .sel(Sel_Saida_Ry), .en(Enable_Saida_Reg));
endmodule

module RAM_II (
  input  in_1,
  input  On_Stop,
  input  Clr,
  output [7:0] out_4
);

  wire clock_1_out, not_1_out;
  wire [7:0] counter_1_q;

  Counter counter_1 (.Q(counter_1_q), .clk(clock_1_out), .clr(Clr));  // open: load, D, count, carry
  Clock clock_1 (.out(clock_1_out));
  assign out_4 = in_1 ? counter_1_q : 8'bz;  // Controlled_Buffer controlled_buffer_1
  not not_1 (not_1_out, in_1);
  RAM_part ram_1 (.addr(counter_1_q), .data(out_4), .sel(On_Stop), .clk(clock_1_out), .ld(not_1_out), .clr(Clr));
endmodule

// PC
module PC_3 (
  input  CLOCK,
  input  CLEAR,
  input  ENABLE_PC,
  output [4:0] \ENDEREÇO 
);

  wire [4:0] adder_1_out;

  Adder #(.width(5)) adder_1 (.a(\ENDEREÇO ), .b(5'b00001), .out(adder_1_out));  // open: cin, cout
  Register #(.width(5)) register_1 (.D(adder_1_out), .en(ENABLE_PC), .Q(\ENDEREÇO ), .clk(CLOCK), .clr(CLEAR));
endmodule

// UC
module Unidade_de_Controle (
  input  [7:0] Entrada_IR,
  input  CLOCK,
  output [4:0] \ENDEREÇO ,
  output [1:0] Saida_Ry,
  output [1:0] Saida_Rx,
  output ULA,
  output STOP,
  output COPIAR_REG,
  output LER_MEM,
  output [3:0] Saida_Op
);

  wire [7:0] ir_1_op__code;

  PC_3 pc_3_1 (.CLOCK(CLOCK), .\ENDEREÇO (\ENDEREÇO ));  // open: CLEAR, ENABLE_PC
  IR ir_1 (
    .IR_Load(1'b1), .Clock(CLOCK), .Entr__IR(Entrada_IR), .Ry(Saida_Ry), .Rx(Saida_Rx),
    .Op__Code(ir_1_op__code));
  DECODIFICADOR decodificador_1 (
    .\Saida_Intrução (Saida_Op), .Ent__UC(ir_1_op__code), .ULA(ULA), .STOP(STOP), .COPIAR_REG(COPIAR_REG),
    .Ler__Mem(LER_MEM));  // open: COPIAR_ACU
endmodule

// DECOD
module DECODIFICADOR (
  input  [7:0] Ent__UC,
  output [3:0] \Saida_Intrução ,
  output ULA,
  output STOP,
  output COPIAR_REG,
  output COPIAR_ACU,
  output Ler__Mem
);

  wire and_2_out;

  and and_1 (ULA, Ent__UC[0], ~Ent__UC[1], ~Ent__UC[2], Ent__UC[3]);  // AND_Gate
  not not_1 (STOP, and_2_out);
  and and_2 (and_2_out, ~Ent__UC[0], Ent__UC[1], ~Ent__UC[2], Ent__UC[3]);  // AND_Gate
  and and_3 (COPIAR_REG, Ent__UC[0], Ent__UC[1], ~Ent__UC[2], Ent__UC[3]);  // AND_Gate
  and and_4 (COPIAR_ACU, ~Ent__UC[0], ~Ent__UC[1], Ent__UC[2], Ent__UC[3]);  // AND_Gate
  and and_5 (Ler__Mem, Ent__UC[0], ~Ent__UC[1], Ent__UC[2], Ent__UC[3]);  // AND_Gate

  assign \Saida_Intrução  = Ent__UC[7:4];
endmodule

module CPU_4 (
  input  Clock
);

  wire decodificador_1_ler__mem, decodificador_1_stop, decodificador_1_ula;
  wire [1:0] ir_1_rx, ir_1_ry;
  wire [3:0] \decodificador_1_saida_intrução ;
  wire [4:0] counter_1_q;
  wire [7:0] banco_de_registradores_1_saida_rx, banco_de_registradores_1_saida_ry, ir_1_op__code, RA_q,
       ram_1_data, ram_2_data, \ula_1_saída_1 ;

  Register #(.trigger("falling")) RA (.D(\ula_1_saída_1 ), .Q(RA_q), .clk(decodificador_1_ula));  // open: en, clr
  Hex_Digit_Display hex_digit_display_1 (.value(RA_q[3:0]));  // open: dp
  Hex_Digit_Display hex_digit_display_2 (.value(RA_q[7:4]));  // open: dp
  ULA ula_1 (
    .Rx(banco_de_registradores_1_saida_rx), .Ry(banco_de_registradores_1_saida_ry),
    .\Saída_1 (\ula_1_saída_1 ));
  BANCO_DE_REGISTRADORES banco_de_registradores_1 (
    .Ent__Registradores(ram_2_data), .Enable(decodificador_1_ler__mem), .Clock(Clock),
    .Sel_Saida_Rx(ir_1_rx), .Sel_Saida_Ry(ir_1_ry), .Enable_Saida_Reg(decodificador_1_ula),
    .Saida_Rx(banco_de_registradores_1_saida_rx), .Saida_Ry(banco_de_registradores_1_saida_ry));  // open: Clear
  Counter #(.width(5), .max('h1f)) counter_1 (.Q(counter_1_q), .clk(Clock));  // open: load, D, count, carry, clr
  DECODIFICADOR decodificador_1 (
    .\Saida_Intrução (\decodificador_1_saida_intrução ), .Ent__UC(ir_1_op__code), .ULA(decodificador_1_ula),
    .STOP(decodificador_1_stop), .Ler__Mem(decodificador_1_ler__mem));  // open: COPIAR_REG, COPIAR_ACU
  RAM_part #(.addrWidth(5)) ram_1 (
    .addr(counter_1_q), .data(ram_1_data), .sel(decodificador_1_stop));  // open: clk, ld, clr
  IR ir_1 (.IR_Load(1'b1), .Clock(Clock), .Entr__IR(ram_1_data), .Ry(ir_1_ry), .Rx(ir_1_rx), .Op__Code(ir_1_op__code));
  RAM_part #(.addrWidth(4)) ram_2 (
    .addr(\decodificador_1_saida_intrução ), .data(ram_2_data));  // open: sel, clk, ld, clr

  // Notes on the sheet:
  //   PC
endmodule

// RA
module ACUMULADOR (
  input  [7:0] ENTRADA_RA,
  input  Clock,
  output [7:0] Saida_Acumulador
);

  Register #(.trigger("falling")) register_1 (
    .D(ENTRADA_RA), .en(Clock), .Q(Saida_Acumulador), .clk(Clock));  // open: clr
endmodule

module CPU (
  input  [7:0] Entrada_IR,
  input  Clock,
  input  [7:0] Entrada_Reg,
  output [4:0] \ENDEREÇO ,
  output STOP,
  output [3:0] Saida_1,
  output [3:0] Saida_2,
  output [3:0] Saida__Op
);

  wire unidade_de_controle_1_ler_mem, unidade_de_controle_1_ula;
  wire [1:0] unidade_de_controle_1_saida_rx, unidade_de_controle_1_saida_ry;
  wire [7:0] banco_de_registradores_1_saida_rx, banco_de_registradores_1_saida_ry, \ula_1_saída_1 ;

  Register #(.trigger("falling")) RA (
    .D(\ula_1_saída_1 ), .Q({Saida_2, Saida_1}), .clk(unidade_de_controle_1_ula));  // open: en, clr
  ULA ula_1 (
    .Rx(banco_de_registradores_1_saida_rx), .Ry(banco_de_registradores_1_saida_ry),
    .\Saída_1 (\ula_1_saída_1 ));
  BANCO_DE_REGISTRADORES banco_de_registradores_1 (
    .Ent__Registradores(Entrada_Reg), .Enable(unidade_de_controle_1_ler_mem), .Clock(Clock),
    .Sel_Saida_Rx(unidade_de_controle_1_saida_rx), .Sel_Saida_Ry(unidade_de_controle_1_saida_ry),
    .Enable_Saida_Reg(unidade_de_controle_1_ula), .Saida_Rx(banco_de_registradores_1_saida_rx),
    .Saida_Ry(banco_de_registradores_1_saida_ry));  // open: Clear
  Unidade_de_Controle unidade_de_controle_1 (
    .CLOCK(Clock), .Entrada_IR(Entrada_IR), .Saida_Ry(unidade_de_controle_1_saida_ry),
    .Saida_Rx(unidade_de_controle_1_saida_rx), .Saida_Op(Saida__Op), .\ENDEREÇO (\ENDEREÇO ),
    .ULA(unidade_de_controle_1_ula), .STOP(STOP), .LER_MEM(unidade_de_controle_1_ler_mem));  // open: COPIAR_REG
endmodule

module COMPUTADOR (
);

  wire clock_1_out, cpu_1_stop, not_1_out;
  wire [3:0] cpu_1_saida_1, cpu_1_saida_2, cpu_1_saida__op;
  wire [4:0] \cpu_1_endereço ;
  wire [7:0] ram_1_data, ram_2_data;

  Clock clock_1 (.out(clock_1_out));
  CPU cpu_1 (
    .Clock(clock_1_out), .\ENDEREÇO (\cpu_1_endereço ), .Entrada_IR(ram_1_data), .Entrada_Reg(ram_2_data),
    .Saida__Op(cpu_1_saida__op), .STOP(cpu_1_stop), .Saida_1(cpu_1_saida_1), .Saida_2(cpu_1_saida_2));
  not not_1 (not_1_out, cpu_1_stop);
  RAM_part #(.addrWidth(5)) ram_1 (
    .addr(\cpu_1_endereço ), .data(ram_1_data), .sel(cpu_1_stop), .clr(not_1_out));  // open: clk, ld
  RAM_part #(.addrWidth(4)) ram_2 (.addr(cpu_1_saida__op), .data(ram_2_data));  // open: sel, clk, ld, clr
  Hex_Digit_Display hex_digit_display_1 (.value(cpu_1_saida_2));  // open: dp
  Hex_Digit_Display hex_digit_display_2 (.value(cpu_1_saida_1));  // open: dp

  // Notes on the sheet:
  //   MEMÓRIA DE PROGRAMA
  //   MEMÓRIA DE DADOS
  //   VALOR CONTIDO NO RA
endmodule
